// Logisim project PROGRAM-10.circ as structural Verilog: 1 circuit, main circuit main
// A
module main (
  input  A,
  input  B,
  input  C_IN,
  output DIFFERENCE,
  output BO
);

  wire and_1_out, and_2_out, not_1_out, not_2_out, xor_1_out;

  not not_1 (not_1_out, B);
  xor xor_1 (xor_1_out, B, C_IN);
  and and_1 (and_1_out, not_1_out, C_IN);
  xor xor_2 (DIFFERENCE, A, xor_1_out);
  not not_2 (not_2_out, xor_1_out);
  and and_2 (and_2_out, not_2_out, A);
  or or_1 (BO, and_2_out, and_1_out);
endmodule
