// Logisim project PROGRAM-11.circ as structural Verilog: 2 circuits, main circuit main
module main (
  input  in_1,
  input  [1:0] in_2,
  output out_3,
  output out_4,
  output out_5,
  output out_6
);

  Demultiplexer #(.select(2)) demultiplexer_1 (
    .out0(out_3), .out1(out_4), .out2(out_5), .out3(out_6), .in(in_1), .sel(in_2));  // open: en
endmodule

module F_A_B_C (
  input  A,
  input  B,
  input  C,
  output F
);

  wire and_1_out, and_2_out, and_3_out, and_4_out, not_1_out, not_2_out, not_3_out, or_1_out;

  not not_1 (not_1_out, A);
  not not_2 (not_2_out, B);
  and and_1 (and_1_out, not_1_out, not_2_out);
  not not_3 (not_3_out, C);
  and and_2 (and_2_out, and_1_out, C);
  and and_3 (and_3_out, B, not_3_out);
  or or_1 (or_1_out, and_2_out, and_3_out);
  and and_4 (and_4_out, A, B);
  or or_2 (F, or_1_out, and_4_out);
endmodule
