// Logisim project PROGRAM-14.circ as structural Verilog: 2 circuits, main circuit main
module main (
  input  [3:0] in_1,
  input  [3:0] B,
  output out_3,
  output out_4,
  output out_5
);

  Comparator #(.width(4)) comparator_1 (.a(in_1), .b(B), .gt(out_3), .eq(out_4), .lt(out_5));

  // Notes on the sheet:
  //   A
endmodule

module F_ABC (
  input  A,
  input  B,
  input  C,
  output D
);

  wire and_1_out, not_1_out;

  not not_1 (not_1_out, A);
  and and_1 (and_1_out, not_1_out, B);
  or or_1 (D, C, and_1_out);
endmodule
