// Logisim project PROGRAM-17.circ as structural Verilog: 1 circuit, main circuit main
module main (
  input  in_1
);

  wire clock_1_out, d_ff_1_q, d_ff_2_q, d_ff_3_q;

  Clock clock_1 (.out(clock_1_out));
  D_Flip_Flop d_ff_1 (.clk(clock_1_out), .D(in_1), .Q(d_ff_1_q));  // open: Qn, preset, en, reset
  LED led_1 ();  // open: in
  LED led_2 ();  // open: in
  D_Flip_Flop d_ff_2 (.clk(clock_1_out), .D(d_ff_1_q), .Q(d_ff_2_q));  // open: Qn, preset, en, reset
  // AND_Gate and_1 has open pins: in0=d_ff_1_q, in4=d_ff_2_q, out=open
  D_Flip_Flop d_ff_3 (.clk(clock_1_out), .Q(d_ff_3_q));  // open: D, Qn, preset, en, reset
  LED led_3 ();  // open: in

  // Notes on the sheet:
  //   Program 17
endmodule
