// Logisim project PROGRAM-19.circ as structural Verilog: 1 circuit, main circuit main
module main (
  input  c_in,
  input  A,
  input  B,
  input  [1:0] operation,
  output Result,
  output out_6
);

  wire adder_1_out, and_1_out, or_1_out;

  or or_1 (or_1_out, A, B);
  and and_1 (and_1_out, A, B);
  Adder #(.width(1)) adder_1 (.a(A), .b(B), .out(adder_1_out), .cin(c_in), .cout(out_6));
  Multiplexer #(.select(2)) multiplexer_1 (
    .in0(or_1_out), .in1(and_1_out), .in2(adder_1_out), .out(Result), .sel(operation));  // open: in3, en

  // Notes on the sheet:
  //   PROGRAM 19
  //   c-output
endmodule
