// Logisim project PROGRAM-20.circ as structural Verilog: 1 circuit, main circuit main
module main (
  input  in_1,
  input  in_2,
  input  in_3,
  input  in_4,
  input  in_5,
  input  in_6,
  input  in_7,
  input  in_8,
  output S0,
  output S1,
  output S2,
  output S3,
  output S4
);

  Adder #(.width(1)) adder_1 (.a(in_1), .b(in_2), .out(S0));  // open: cin, cout
  Adder #(.width(1)) adder_2 (.a(in_3), .b(in_4), .out(S1));  // open: cin, cout
  Adder #(.width(1)) adder_3 (.a(in_5), .b(in_6), .out(S2));  // open: cin, cout
  Adder #(.width(1)) adder_4 (.a(in_7), .b(in_8), .out(S3), .cout(S4));  // open: cin

  // Notes on the sheet:
  //   PROGRAM 20
endmodule
