// Logisim project PROGRAM-6.circ as structural Verilog
module F_ABCD (
  input  A,
  input  B,
  input  C,
  input  D,
  output F
);

  wire and_1_out, and_2_out, not_1_out, not_2_out;

  not not_1 (not_1_out, B);
  not not_2 (not_2_out, D);
  and and_1 (and_1_out, not_1_out, not_2_out);
  and and_2 (and_2_out, B, D);
  or or_1 (F, and_1_out, and_2_out);
endmodule
