// Logisim project PROGRAM-7.circ as structural Verilog
module SC_AB (
  input  A,
  input  B,
  output S,
  output C
);

  xor xor_1 (S, A, B);
  and and_1 (C, A, A);
endmodule
